// Logisim project ALU.circ as structural Verilog: 3 circuits, main circuit ALU
module ALU (
  input  [31:0] A,
  input  [31:0] B,
  input  [4:0] Shift,
  input  CarryIn,
  input  [3:0] Codop,
  output [31:0] S,
  output [3:0] Flags
);

  wire adder_2_cout, bitselector_1_out, bitselector_2_out, not_1_out, not_4_out, overflow_add_1_v,
       overflow_sub_1_v, subtractor_2_bout;
  wire [4:0] negator_1_out, subtractor_1_out;
  wire [31:0] adder_1_out, adder_2_out, and_1_out, and_2_out, and_3_out, multiplier_1_out, not_2_out,
       not_3_out, or_1_out, shifter_1_out, shifter_2_out, shifter_3_out, shifter_4_out, subtractor_2_out,
       subtractor_3_out, subtractor_4_out, xor_1_out;

  Subtractor #(.width(5)) subtractor_1 (.a(Shift), .b(5'b00001), .out(subtractor_1_out));  // open: bin, bout
  BitSelector #(.width(32)) bitselector_1 (.in(B), .out(bitselector_1_out), .sel(subtractor_1_out));
  not not_1 (not_1_out, CarryIn);
  assign and_1_out = B & A;  // AND_Gate and_1, 32 bits wide
  assign xor_1_out = B ^ A;  // XOR_Gate xor_1, 32 bits wide
  Shifter #(.width(32)) shifter_1 (.in(B), .\dist (Shift), .out(shifter_1_out));
  Shifter #(.shift("ar"), .width(32)) shifter_2 (.in(B), .\dist (Shift), .out(shifter_2_out));
  Shifter #(.shift("ar"), .width(32)) shifter_3 (.in(B), .\dist (Shift), .out(shifter_3_out));
  Adder #(.width(32)) adder_1 (.a(B), .b(A), .out(adder_1_out), .cin(CarryIn));  // open: cout
  Subtractor #(.width(32)) subtractor_2 (
    .a(B), .b(A), .out(subtractor_2_out), .bin(not_1_out), .bout(subtractor_2_bout));
  Shifter #(.shift("rr"), .width(32)) shifter_4 (.in(B), .\dist (Shift), .out(shifter_4_out));
  assign and_2_out = B & A;  // AND_Gate and_2, 32 bits wide
  Subtractor #(.width(32)) subtractor_3 (.a({32{1'b0}}), .b(A), .out(subtractor_3_out));  // open: bin, bout
  Subtractor #(.width(32)) subtractor_4 (.a(B), .b(A), .out(subtractor_4_out));  // open: bin, bout
  Adder #(.width(32)) adder_2 (.a(B), .b(A), .out(adder_2_out), .cout(adder_2_cout));  // open: cin
  assign or_1_out = B | A;  // OR_Gate or_1, 32 bits wide
  Multiplier #(.width(32)) multiplier_1 (.a(B), .b(A), .out(multiplier_1_out));  // open: cin, cout
  assign not_2_out = ~A;  // NOT_Gate not_2, 32 bits wide
  assign not_3_out = ~A;  // NOT_Gate not_3, 32 bits wide
  Negator #(.width(5)) negator_1 (.in(Shift), .out(negator_1_out));
  BitSelector #(.width(32)) bitselector_2 (.in(B), .out(bitselector_2_out), .sel(negator_1_out));
  assign and_3_out = B & not_2_out;  // AND_Gate and_3, 32 bits wide
  not not_4 (not_4_out, subtractor_2_bout);
  Multiplexer #(.select(4), .width(32)) multiplexer_1 (
    .in0(and_1_out), .in1(xor_1_out), .in2(shifter_1_out), .in3(shifter_2_out), .in4(shifter_3_out),
    .in5(adder_1_out), .in6(subtractor_2_out), .in7(shifter_4_out), .in8(and_2_out), .in9(subtractor_3_out),
    .in10(subtractor_4_out), .in11(adder_2_out), .in12(or_1_out), .in13(multiplier_1_out), .in14(and_3_out),
    .in15(not_3_out), .out({Flags[3], S[30:0]}), .sel(Codop));
  Multiplexer #(.select(4)) multiplexer_2 (
    .in0(1'b0), .in1(1'b0), .in2(bitselector_2_out), .in3(bitselector_1_out), .in4(bitselector_1_out),
    .in5(adder_2_cout), .in6(not_4_out), .in7(shifter_4_out[31]), .in8(1'b0), .in9(1'b0), .in10(not_4_out),
    .in11(adder_2_cout), .in12(1'b0), .in13(1'b0), .in14(1'b0), .in15(1'b0), .out(Flags[1]), .sel(Codop));
  Multiplexer #(.select(4)) multiplexer_3 (
    .in0(1'b0), .in1(1'b0), .in2(1'b0), .in3(1'b0), .in4(1'b0), .in5(overflow_add_1_v),
    .in6(overflow_sub_1_v), .in7(1'b0), .in8(1'b0), .in9(overflow_sub_1_v), .in10(overflow_sub_1_v),
    .in11(overflow_add_1_v), .in12(1'b0), .in13(1'b0), .in14(1'b0), .in15(1'b0), .out(Flags[0]), .sel(Codop));
  Comparator #(.width(32)) comparator_1 (.a({Flags[3], S[30:0]}), .b({32{1'b0}}), .eq(Flags[2]));  // open: gt, lt
  OverFlow_Add overflow_add_1 (.A(A[31]), .B(B[31]), .S(Flags[3]), .V(overflow_add_1_v));
  OverFlow_Sub overflow_sub_1 (.A(A[31]), .B(B[31]), .S(Flags[3]), .V(overflow_sub_1_v));

  assign S[31] = Flags[3];

  // Notes on the sheet:
  //   Note: for ROR, C = N
  //   Note 2: assume that shift > 0 for LSL and LSR
endmodule

module OverFlow_Add (
  input  A,
  input  B,
  input  S,
  output V
);

  wire and_1_out, and_2_out, not_1_out, not_2_out, not_3_out;

  not not_1 (not_1_out, A);
  not not_2 (not_2_out, B);
  not not_3 (not_3_out, S);
  and and_1 (and_1_out, not_1_out, not_2_out, S);
  or or_1 (V, and_1_out, and_2_out);
  and and_2 (and_2_out, A, B, not_3_out);
endmodule

module OverFlow_Sub (
  input  A,
  input  B,
  input  S,
  output V
);

  wire and_1_out, and_2_out, not_1_out, not_2_out, not_3_out;

  not not_1 (not_1_out, A);
  not not_2 (not_2_out, B);
  not not_3 (not_3_out, S);
  and and_1 (and_1_out, not_1_out, B, not_3_out);
  or or_1 (V, and_1_out, and_2_out);
  and and_2 (and_2_out, A, not_2_out, S);
endmodule
