// Logisim project Ctl_Conditional.circ as structural Verilog: 1 circuit, main circuit Conditional
module Conditional (
  input  Enable,
  input  [15:0] Instruction,
  input  Z,
  input  C,
  input  N,
  input  V,
  output [10:0] Offset,
  output Verified
);

  wire and_1_out, and_2_out, multiplexer_1_out, multiplexer_3_out, not_1_out, not_2_out, not_3_out,
       not_4_out, not_5_out, or_1_out, or_2_out, xnor_1_out, xor_1_out;
  wire [10:0] bit_extender_1_out, multiplexer_2_out;

  not not_1 (not_1_out, Z);
  not not_2 (not_2_out, C);
  not not_3 (not_3_out, N);
  not not_4 (not_4_out, V);
  and and_1 (and_1_out, C, not_1_out);
  or or_1 (or_1_out, not_2_out, Z);
  xnor xnor_1 (xnor_1_out, N, V);
  xor xor_1 (xor_1_out, N, V);
  and and_2 (and_2_out, not_1_out, xnor_1_out);
  or or_2 (or_2_out, Z, xor_1_out);
  assign bit_extender_1_out = {{3{Instruction[7]}}, Instruction[7:0]};  // Bit_Extender bit_extender_1
  Multiplexer #(.select(4)) multiplexer_1 (
    .in0(Z), .in1(not_1_out), .in2(C), .in3(not_2_out), .in4(N), .in5(not_3_out), .in6(V), .in7(not_4_out),
    .in8(and_1_out), .in9(or_1_out), .in10(xnor_1_out), .in11(xor_1_out), .in12(and_2_out), .in13(or_2_out),
    .in14(1'b1), .out(multiplexer_1_out), .sel(Instruction[11:8]));  // open: in15
  Multiplexer #(.width(11)) multiplexer_2 (
    .in0(bit_extender_1_out), .in1(Instruction[10:0]), .out(multiplexer_2_out), .sel(Instruction[13]));
  Multiplexer multiplexer_3 (.in0(multiplexer_1_out), .in1(1'b1), .out(multiplexer_3_out), .sel(not_5_out));
  not not_5 (not_5_out, Instruction[12]);
  Pull_Resistor pull_resistor_1 (.node(Offset));
  assign Offset = Verified ? multiplexer_2_out : 11'bz;  // Controlled_Buffer controlled_buffer_1
  Multiplexer multiplexer_4 (.in0(1'b0), .in1(multiplexer_3_out), .out(Verified), .sel(Enable));

  // Other names for the same wires on the sheet: En = Enable; Im8[7:0] = Instruction[7:0];
  //   Im11[10:0] = Instruction[10:0]; Ins[15:0] = Instruction; Cond[3:0] = Instruction[11:8]; B12 = Instruction[12];
  //   cond1 = Instruction[13]; Ver = Verified
endmodule
