// Logisim project Ctl_Load_Store.circ as structural Verilog: 1 circuit, main circuit Load_Store
module Load_Store (
  input  Enable,
  input  [15:0] Instruction,
  input  Clk,
  input  Reset,
  input  [31:0] Stack_Pointer,
  output Store,
  output Load,
  output PC_Hold,
  output [2:0] Rmd,
  output [31:0] RAM_Addr
);

  wire and_1_out, load1, or_1_out, s1, s2;
  wire [31:0] adder_1_out, off;

  or or_1 (or_1_out, s1, s2);
  D_Flip_Flop d_ff_1 (.D(and_1_out), .clk(Clk), .Q(PC_Hold), .reset(Reset));  // open: Qn, preset
  and and_1 (and_1_out, or_1_out, Enable);
  assign off = {{24{1'b0}}, Instruction[7:0]};  // Bit_Extender bit_extender_1
  Multiplexer #(.width(3)) multiplexer_1 (.in0(3'b000), .in1(Instruction[10:8]), .out(Rmd), .sel(Enable));
  Comparator #(.mode("unsigned"), .width(5)) comparator_1 (
    .a(Instruction[15:11]), .b(5'b10010), .eq(s1));  // open: gt, lt
  Comparator #(.mode("unsigned"), .width(5)) comparator_2 (
    .a(Instruction[15:11]), .b(5'b10011), .eq(s2));  // open: gt, lt
  and and_2 (Store, s1, Enable);
  and and_3 (load1, s2, Enable);
  D_Flip_Flop d_ff_2 (.D(load1), .clk(Clk), .Q(Load), .reset(Reset));  // open: Qn, preset
  Adder #(.width(32)) adder_1 (.a(Stack_Pointer), .b(off), .out(adder_1_out));  // open: cin, cout
  Multiplexer #(.width(32)) multiplexer_2 (.in0({32{1'b0}}), .in1(adder_1_out), .out(RAM_Addr), .sel(Enable));

  // Other names for the same wires on the sheet: en = Enable; PcH = PC_Hold; Sp[31:0] = Stack_Pointer

  // Notes on the sheet:
  //   Delay load and hold PC for 1 cycle for the RAM to send out requested data 
endmodule
