// Logisim project Ctl_Opcode_Decoder.circ as structural Verilog: 1 circuit, main circuit Opcode_Decoder
module Opcode_Decoder (
  input  [5:0] Opcode,
  output Shift,
  output Data_Processing,
  output Load_Store,
  output SP_Address,
  output Conditional
);

  wire decoder_1_out0, decoder_1_out1, decoder_1_out2, decoder_1_out3, decoder_1_out4, decoder_1_out5,
       decoder_1_out6, decoder_1_out7, decoder_1_out24, decoder_1_out25, decoder_1_out26, decoder_1_out27,
       decoder_1_out28, decoder_1_out29, decoder_1_out30, decoder_1_out31, decoder_1_out32, decoder_1_out33,
       decoder_1_out34, decoder_1_out35, decoder_1_out36, decoder_1_out37, decoder_1_out38, decoder_1_out39,
       decoder_1_out52, decoder_1_out53, decoder_1_out54, decoder_1_out55;

  Decoder #(.select(6)) decoder_1 (
    .out0(decoder_1_out0), .out1(decoder_1_out1), .out2(decoder_1_out2), .out3(decoder_1_out3),
    .out4(decoder_1_out4), .out5(decoder_1_out5), .out6(decoder_1_out6), .out7(decoder_1_out7),
    .out16(Data_Processing), .out24(decoder_1_out24), .out25(decoder_1_out25), .out26(decoder_1_out26),
    .out27(decoder_1_out27), .out28(decoder_1_out28), .out29(decoder_1_out29), .out30(decoder_1_out30),
    .out31(decoder_1_out31), .out32(decoder_1_out32), .out33(decoder_1_out33), .out34(decoder_1_out34),
    .out35(decoder_1_out35), .out36(decoder_1_out36), .out37(decoder_1_out37), .out38(decoder_1_out38),
    .out39(decoder_1_out39), .out44(SP_Address), .out52(decoder_1_out52), .out53(decoder_1_out53),
    .out54(decoder_1_out54), .out55(decoder_1_out55), .sel(Opcode));  // open: out8, out9, out10, out11, out12, out13, out14, out15, out17, out18, out19, out20, out21, out22, out23, out40, out41, out42, out43, out45, out46, out47, out48, out49, out50, out51, out56, out57, out58, out59, out60, out61, out62, out63, en
  or or_1 (Conditional, decoder_1_out52, decoder_1_out53, decoder_1_out54, decoder_1_out55);
  or or_2 (Shift, decoder_1_out0, decoder_1_out1, decoder_1_out2, decoder_1_out3, decoder_1_out4, decoder_1_out5, decoder_1_out6, decoder_1_out7);
  or or_3 (Load_Store, decoder_1_out24, decoder_1_out25, decoder_1_out26, decoder_1_out27, decoder_1_out28, decoder_1_out29, decoder_1_out30, decoder_1_out31, decoder_1_out32, decoder_1_out33, decoder_1_out34, decoder_1_out35, decoder_1_out36, decoder_1_out37, decoder_1_out38, decoder_1_out39);

  // Notes on the sheet:
  //   SP Address
  //   Shift, add, sub, mov
  //   Data Processing
  //   Load/Store
  //   Conditional branch
endmodule
