// Logisim project Ctl_SP_Address.circ as structural Verilog: 1 circuit, main circuit SP_Address
module SP_Address (
  input  [31:0] Stack_Pointer,
  input  [15:0] Instruction,
  input  Enable,
  output [31:0] New_Stack_Pointer,
  output Write_Enable
);

  wire [31:0] adder_1_out, B, bit_extender_1_out, multiplexer_1_out, subtractor_1_out;

  Adder #(.width(32)) adder_1 (.a(Stack_Pointer), .b(B), .out(adder_1_out));  // open: cin, cout
  Multiplexer #(.width(32)) multiplexer_1 (
    .in0(adder_1_out), .in1(subtractor_1_out), .out(multiplexer_1_out), .sel(Instruction[7]));
  Subtractor #(.width(32)) subtractor_1 (.a(Stack_Pointer), .b(B), .out(subtractor_1_out));  // open: bin, bout
  assign bit_extender_1_out = {{25{1'b0}}, Instruction[6:0]};  // Bit_Extender bit_extender_1
  Shifter #(.width(32)) shifter_1 (.in(bit_extender_1_out), .\dist (5'b00010), .out(B));
  Multiplexer #(.width(32)) multiplexer_2 (
    .in0(Stack_Pointer), .in1(multiplexer_1_out), .out(New_Stack_Pointer), .sel(Enable));

  assign Write_Enable = Enable;

  // Other names for the same wires on the sheet: En = Enable; Op_Select = Instruction[7]

  // Notes on the sheet:
  //   Pull output low on Enable = 0
endmodule
