// Logisim project Ctl_Shift_Add_Sub_Mov.circ as structural Verilog: 1 circuit, main circuit Shift_Add_Sub_Mov
module Shift_Add_Sub_Mov (
  input  [15:0] Instruction,
  input  Enable,
  output [3:0] Flags_Update_Mask,
  output Carry,
  output [2:0] Rm,
  output [4:0] Imm5,
  output Imm32_Enable,
  output [2:0] Rn,
  output [2:0] Rd,
  output [31:0] Imm32,
  output [3:0] ALU_Opcode
);

  wire ADD1_R, ADD2_8, ADD3_I, ASR, CMP, demultiplexer_1_out0, demultiplexer_1_out1, demultiplexer_1_out2,
       demultiplexer_1_out3, demultiplexer_1_out4, demultiplexer_1_out5, demultiplexer_1_out6,
       demultiplexer_1_out7, demultiplexer_1_out8, demultiplexer_1_out9, demultiplexer_1_out10,
       demultiplexer_1_out11, demultiplexer_1_out16, demultiplexer_1_out17, demultiplexer_1_out18,
       demultiplexer_1_out19, demultiplexer_1_out20, demultiplexer_1_out21, demultiplexer_1_out22,
       demultiplexer_1_out23, demultiplexer_1_out24, demultiplexer_1_out25, demultiplexer_1_out26,
       demultiplexer_1_out27, demultiplexer_1_out28, demultiplexer_1_out29, demultiplexer_1_out30,
       demultiplexer_1_out31, GLOB, LSL, LSR, MOVE, or_9_out, or_10_out, SUB1_I, SUB2_8, SUB3_R;
  wire [2:0] multiplexer_2_out, multiplexer_4_out;
  wire [3:0] ALU, F, pull_resistor_1_node, pull_resistor_2_node, pull_resistor_3_node, pull_resistor_4_node,
       pull_resistor_5_node, pull_resistor_6_node, pull_resistor_7_node, pull_resistor_8_node,
       pull_resistor_9_node, pull_resistor_10_node, pull_resistor_11_node;
  wire [3:3] NZC, NZCV;
  wire [31:0] bit_extender_1_out, bit_extender_2_out, multiplexer_1_out, multiplexer_3_out, negator_1_out;

  and and_1 (GLOB, Instruction[14], Instruction[15]);
  Demultiplexer #(.select(5)) demultiplexer_1 (
    .out0(demultiplexer_1_out0), .out1(demultiplexer_1_out1), .out2(demultiplexer_1_out2),
    .out3(demultiplexer_1_out3), .out4(demultiplexer_1_out4), .out5(demultiplexer_1_out5),
    .out6(demultiplexer_1_out6), .out7(demultiplexer_1_out7), .out8(demultiplexer_1_out8),
    .out9(demultiplexer_1_out9), .out10(demultiplexer_1_out10), .out11(demultiplexer_1_out11),
    .out12(ADD1_R), .out13(SUB3_R), .out14(ADD3_I), .out15(SUB1_I), .out16(demultiplexer_1_out16),
    .out17(demultiplexer_1_out17), .out18(demultiplexer_1_out18), .out19(demultiplexer_1_out19),
    .out20(demultiplexer_1_out20), .out21(demultiplexer_1_out21), .out22(demultiplexer_1_out22),
    .out23(demultiplexer_1_out23), .out24(demultiplexer_1_out24), .out25(demultiplexer_1_out25),
    .out26(demultiplexer_1_out26), .out27(demultiplexer_1_out27), .out28(demultiplexer_1_out28),
    .out29(demultiplexer_1_out29), .out30(demultiplexer_1_out30), .out31(demultiplexer_1_out31), .in(1'b1),
    .sel(Instruction[13:9]));
  Pull_Resistor pull_resistor_1 (.node(pull_resistor_1_node));
  assign pull_resistor_1_node = LSL ? 4'b0010 : 4'bz;  // Controlled_Buffer controlled_buffer_1
  Pull_Resistor pull_resistor_2 (.node(pull_resistor_2_node));
  assign pull_resistor_2_node = LSR ? 4'b0011 : 4'bz;  // Controlled_Buffer controlled_buffer_2
  Pull_Resistor pull_resistor_3 (.node(pull_resistor_3_node));
  assign pull_resistor_3_node = ASR ? 4'b0100 : 4'bz;  // Controlled_Buffer controlled_buffer_3
  Pull_Resistor pull_resistor_4 (.node(pull_resistor_4_node));
  assign pull_resistor_4_node = ADD1_R ? 4'b0101 : 4'bz;  // Controlled_Buffer controlled_buffer_4
  Pull_Resistor pull_resistor_5 (.node(pull_resistor_5_node));
  assign pull_resistor_5_node = SUB3_R ? 4'b0110 : 4'bz;  // Controlled_Buffer controlled_buffer_5
  Pull_Resistor pull_resistor_6 (.node(pull_resistor_6_node));
  assign pull_resistor_6_node = ADD3_I ? 4'b0101 : 4'bz;  // Controlled_Buffer controlled_buffer_6
  Pull_Resistor pull_resistor_7 (.node(pull_resistor_7_node));
  assign pull_resistor_7_node = SUB1_I ? 4'b0110 : 4'bz;  // Controlled_Buffer controlled_buffer_7
  Pull_Resistor pull_resistor_8 (.node(pull_resistor_8_node));
  assign pull_resistor_8_node = MOVE ? 4'b1001 : 4'bz;  // Controlled_Buffer controlled_buffer_8
  Pull_Resistor pull_resistor_9 (.node(pull_resistor_9_node));
  assign pull_resistor_9_node = CMP ? 4'b1010 : 4'bz;  // Controlled_Buffer controlled_buffer_9
  Pull_Resistor pull_resistor_10 (.node(pull_resistor_10_node));
  assign pull_resistor_10_node = ADD2_8 ? 4'b0101 : 4'bz;  // Controlled_Buffer controlled_buffer_10
  Pull_Resistor pull_resistor_11 (.node(pull_resistor_11_node));
  assign pull_resistor_11_node = SUB2_8 ? 4'b0110 : 4'bz;  // Controlled_Buffer controlled_buffer_11
  assign bit_extender_1_out = {{24{1'b0}}, Instruction[7:0]};  // Bit_Extender bit_extender_1
  or or_1 (LSR, demultiplexer_1_out4, demultiplexer_1_out5, demultiplexer_1_out6, demultiplexer_1_out7);
  or or_2 (ASR, demultiplexer_1_out8, demultiplexer_1_out9, demultiplexer_1_out10, demultiplexer_1_out11);
  or or_3 (MOVE, demultiplexer_1_out16, demultiplexer_1_out17, demultiplexer_1_out18, demultiplexer_1_out19);
  or or_4 (CMP, demultiplexer_1_out20, demultiplexer_1_out21, demultiplexer_1_out22, demultiplexer_1_out23);
  or or_5 (ADD2_8, demultiplexer_1_out24, demultiplexer_1_out25, demultiplexer_1_out26, demultiplexer_1_out27);
  or or_6 (SUB2_8, demultiplexer_1_out28, demultiplexer_1_out29, demultiplexer_1_out30, demultiplexer_1_out31);
  assign ALU = pull_resistor_1_node | pull_resistor_2_node | pull_resistor_3_node | pull_resistor_4_node | pull_resistor_5_node | pull_resistor_6_node | pull_resistor_7_node | pull_resistor_8_node | pull_resistor_9_node | pull_resistor_10_node | pull_resistor_11_node;  // OR_Gate or_7, 4 bits wide
  Negator #(.width(32)) negator_1 (.in(bit_extender_1_out), .out(negator_1_out));
  or or_8 (LSL, demultiplexer_1_out0, demultiplexer_1_out1, demultiplexer_1_out2, demultiplexer_1_out3);
  assign bit_extender_2_out = {{29{1'b0}}, Instruction[8:6]};  // Bit_Extender bit_extender_2
  Multiplexer #(.width(32)) multiplexer_1 (
    .in0(bit_extender_1_out), .in1(negator_1_out), .out(multiplexer_1_out), .sel(MOVE));
  or or_9 (or_9_out, SUB1_I, SUB2_8, SUB3_R);
  or or_10 (or_10_out, MOVE, CMP, ADD2_8, SUB2_8, ADD3_I, SUB1_I);
  Multiplexer #(.width(3)) multiplexer_2 (
    .in0(Instruction[2:0]), .in1(Instruction[10:8]), .out(multiplexer_2_out), .sel(Instruction[13]));
  Multiplexer #(.width(32)) multiplexer_3 (
    .in0(bit_extender_2_out), .in1(multiplexer_1_out), .out(multiplexer_3_out), .sel(Instruction[13]));
  assign Flags_Update_Mask = Enable ? F : 4'bz;  // Controlled_Buffer controlled_buffer_12
  assign Carry = Enable ? or_9_out : 1'bz;  // Controlled_Buffer controlled_buffer_13
  Pull_Resistor pull_resistor_12 (.node(Carry));
  assign Rm = Enable ? Instruction[8:6] : 3'bz;  // Controlled_Buffer controlled_buffer_14
  assign Imm5 = Enable ? Instruction[10:6] : 5'bz;  // Controlled_Buffer controlled_buffer_15
  Pull_Resistor pull_resistor_13 (.node(Imm5));
  Pull_Resistor pull_resistor_14 (.node(Imm32_Enable));
  assign Imm32_Enable = Enable ? or_10_out : 1'bz;  // Controlled_Buffer controlled_buffer_16
  Multiplexer #(.width(3)) multiplexer_4 (
    .in0(Instruction[5:3]), .in1(Instruction[10:8]), .out(multiplexer_4_out), .sel(Instruction[13]));
  assign Rd = Enable ? multiplexer_2_out : 3'bz;  // Controlled_Buffer controlled_buffer_17
  Pull_Resistor pull_resistor_15 (.node(Rd));
  assign Imm32 = Enable ? multiplexer_3_out : 32'bz;  // Controlled_Buffer controlled_buffer_18
  Pull_Resistor pull_resistor_16 (.node(Imm32));
  assign ALU_Opcode = Enable ? ALU : 4'bz;  // Controlled_Buffer controlled_buffer_19
  Pull_Resistor pull_resistor_17 (.node(ALU_Opcode));
  Pull_Resistor pull_resistor_18 (.node(Flags_Update_Mask));
  Pull_Resistor pull_resistor_19 (.node(Rm));
  assign Rn = Enable ? multiplexer_4_out : 3'bz;  // Controlled_Buffer controlled_buffer_20
  Pull_Resistor pull_resistor_20 (.node(Rn));
  or or_11 (NZC[3], LSL, LSR, ASR);
  assign F = {{3{NZC[3]}}, 1'b0} | {4{NZCV[3]}} | {{2{MOVE}}, 2'b00};  // OR_Gate or_12, 4 bits wide
  or or_13 (NZCV[3], ADD1_R, SUB3_R, ADD3_I, SUB1_I, CMP, ADD2_8, SUB2_8);

  // Other names for the same wires on the sheet: E = Enable; INS[15:0] = Instruction; B13 = Instruction[13];
  //   NZ[3:2] = {2{MOVE}}; NZC[2:1] = {2{NZC[3]}}; NZCV[2:0] = {3{NZCV[3]}}

  // Notes on the sheet:
  //   NZ
  //   NZC
  //   NZCV
endmodule
